# Fritzing sketch FT232RL Writer (saved by Fritzing 0.9.4)
breadboards: 1

parts:
  U1 = attiny85 [package=dip]
  パーツ1 = FTDI Basic Programmer

nets:
  N1: U1.Pin_1, パーツ1.CTS
  N2: U1.Pin_4, パーツ1.GND
  N3: U1.Pin_5, パーツ1.TXO
  N4: U1.Pin_6, パーツ1.RXI
  N5: U1.Pin_7, パーツ1.DTR
  N6: U1.Pin_8, パーツ1.POWER

notes:
  ftavrw.exe -pa3410
